# Fritzing sketch allumage automatique (saved by Fritzing 0.9.2b)
breadboards: 1

parts:
  U1 = ATTINY45 [package=dip]
  R1 = Photocell (LDR) [package=THT]
  R2 = Resistor [tolerance=±5% resistance=10k package=THT]
  U2 = TLP621 [package=THT]
  U3 = RELAY [package=relay-g5q]
  Power_plug1 = Power plug
  VCC1 = Battery
  LED1 = LED - 5mm [color="Red (633nm)" package="5 mm [THT]"]

nets:
  N1: U1.PB5(NRES), R1.pin_0, R2.Pin_1
  GND: U1.GND, R2.Pin_0, U2.Pin_2, U2.Pin_3, Power_plug1.GND, VCC1.-, LED1.cathode
  N2: U1.PB0(MOSI), U2.Pin_1
  N3: U1.VCC, R1.pin_1
  N4: U2.Pin_4, U3.COIL1
  N5: U3.COIL2, Power_plug1.VCC
  N6: U3.MAIN, VCC1.+
  N7: U3.NO, LED1.anode

// code stored in the sketch: allumage automatique.ino
const int relais = 0; // la LED est liée à la broche digitale 2
float capteur = 3; // la photoresistance est sur la broche 3
int capteurreading; 
void setup() {
  // put your setup code here, to run once:
 pinMode(relais, OUTPUT); // configurer la broche comme sortie
  
}

void loop() {
  // put your main code here, to run repeatedly:

 capteurreading =analogRead(capteur); 



  if (capteurreading<100)
  {
    digitalWrite(relais,HIGH);
    }
      
  else{ // si non (il ya de la lumière)
    digitalWrite(relais,LOW); // éteindre la LED
    
  }
  }
